# Fritzing sketch circuitoAlternativo (saved by Fritzing 0.9.3b)
circuit board: 30cm x 30cm
breadboards: 1

parts:
  U1 = 74HC595 [package="DIP16 [THT]"]
  U2 = 74HC595 [package="DIP16 [THT]"]
  U3 = 74HC595 [package="DIP16 [THT]"]
  U4 = 74HC595 [package="DIP16 [THT]"]
  U5 = 74HC595 [package="DIP16 [THT]"]  # not connected
  U6 = 74HC595 [package="DIP16 [THT]"]

nets:
  GND: U1.GND, U4.GND, U6.GND
  N1: U1.Q7', U2.DS
  N2: U2.Q7', U3.DS
