# Fritzing sketch circuitoMain (saved by Fritzing 0.9.3b)
circuit board: 30cm x 30cm
breadboards: 1

parts:
  U1 = 74HC595 [package="DIP16 [THT]"]
  U2 = 74HC595 [package="DIP16 [THT]"]
  U3 = 74HC595 [package="DIP16 [THT]"]
  U4 = 74HC595 [package="DIP16 [THT]"]
  U5 = 74HC595 [package="DIP16 [THT]"]
  U6 = 74HC595 [package="DIP16 [THT]"]
  U7 = 74HC595 [package="DIP16 [THT]"]
  Q3 = PNP-Transistor [package="TO92 [THT]"]
  Q4 = PNP-Transistor [package="TO92 [THT]"]
  Q5 = PNP-Transistor [package="TO92 [THT]"]
  Q6 = PNP-Transistor [package="TO92 [THT]"]
  Q7 = PNP-Transistor [package="TO92 [THT]"]
  Q8 = PNP-Transistor [package="TO92 [THT]"]
  Q10 = PNP-Transistor [package="TO92 [THT]"]
  Q11 = PNP-Transistor [package="TO92 [THT]"]
  Q12 = PNP-Transistor [package="TO92 [THT]"]
  Q13 = PNP-Transistor [package="TO92 [THT]"]
  Q14 = PNP-Transistor [package="TO92 [THT]"]
  Q15 = PNP-Transistor [package="TO92 [THT]"]
  Q16 = PNP-Transistor [package="TO92 [THT]"]
  Q17 = PNP-Transistor [package="TO92 [THT]"]
  Q18 = PNP-Transistor [package="TO92 [THT]"]
  Q19 = PNP-Transistor [package="TO92 [THT]"]
  Q20 = PNP-Transistor [package="TO92 [THT]"]
  Q21 = PNP-Transistor [package="TO92 [THT]"]
  Q22 = PNP-Transistor [package="TO92 [THT]"]
  Q23 = PNP-Transistor [package="TO92 [THT]"]
  Q24 = PNP-Transistor [package="TO92 [THT]"]
  Q25 = PNP-Transistor [package="TO92 [THT]"]
  Q26 = PNP-Transistor [package="TO92 [THT]"]
  Q27 = PNP-Transistor [package="TO92 [THT]"]
  Q28 = PNP-Transistor [package="TO92 [THT]"]
  Q30 = PNP-Transistor [package="TO92 [THT]"]
  Q31 = PNP-Transistor [package="TO92 [THT]"]
  Q32 = PNP-Transistor [package="TO92 [THT]"]
  Q33 = PNP-Transistor [package="TO92 [THT]"]
  Q34 = PNP-Transistor [package="TO92 [THT]"]
  Q35 = PNP-Transistor [package="TO92 [THT]"]
  Q36 = PNP-Transistor [package="TO92 [THT]"]
  Q37 = PNP-Transistor [package="TO92 [THT]"]
  Q38 = PNP-Transistor [package="TO92 [THT]"]
  Q39 = PNP-Transistor [package="TO92 [THT]"]
  Q40 = PNP-Transistor [package="TO92 [THT]"]
  Q41 = PNP-Transistor [package="TO92 [THT]"]
  Q42 = PNP-Transistor [package="TO92 [THT]"]
  Q43 = PNP-Transistor [package="TO92 [THT]"]
  Q44 = PNP-Transistor [package="TO92 [THT]"]
  Q45 = PNP-Transistor [package="TO92 [THT]"]
  Q46 = PNP-Transistor [package="TO92 [THT]"]
  Q47 = PNP-Transistor [package="TO92 [THT]"]
  Q49 = PNP-Transistor [package="TO92 [THT]"]
  Q50 = PNP-Transistor [package="TO92 [THT]"]
  Q52 = PNP-Transistor [package="TO92 [THT]"]
  Q54 = PNP-Transistor [package="TO92 [THT]"]
  Q55 = PNP-Transistor [package="TO92 [THT]"]
  Q56 = PNP-Transistor [package="TO92 [THT]"]
  Raspberry_Pi_1 = Raspberry Pi 3 [part_number=RPI-3-V1.2]
  Q57 = PNP-Transistor [package="TO92 [THT]"]
  Q58 = PNP-Transistor [package="TO92 [THT]"]
  Q59 = PNP-Transistor [package="TO92 [THT]"]
  Q60 = PNP-Transistor [package="TO92 [THT]"]
  Q61 = PNP-Transistor [package="TO92 [THT]"]
  Q62 = PNP-Transistor [package="TO92 [THT]"]
  Q63 = PNP-Transistor [package="TO92 [THT]"]

nets:
  N1: U1.Q1, Q31.C
  N2: U1.Q2, Q30.C
  N3: U1.Q3, Q43.C
  N4: U1.Q4, Q28.C
  N5: U1.Q5, Q27.C
  N6: U1.Q6, Q41.C
  N7: U1.Q7, Q42.C
  GND: U1.GND, U1.MR, U1.OE, U2.GND, U2.OE, U3.GND, U3.OE, U4.GND, U4.OE, U5.GND, U5.OE, U6.GND, U6.OE, U7.GND, U7.OE, Q25.E, Q26.E, Q27.E, Q28.E, Q30.E, Q31.E, Q32.E, Q33.E, Q34.E, Q35.E, Q36.E, Q37.E, Q38.E, Q39.E, Q40.E, Q41.E, Q42.E, Q43.E, Q45.E, Raspberry_Pi_1.GND, Q57.E, Q61.E, Q63.E
  N8: U1.Q7', U2.DS
  N9: U1.SH_CP, U2.SH_CP, U3.SH_CP, U4.SH_CP, U5.SH_CP, U6.SH_CP, U7.SH_CP, Raspberry_Pi_1.GPIO5
  N10: U1.ST_CP, U2.ST_CP, U3.ST_CP, U4.ST_CP, U5.ST_CP, U6.ST_CP, U7.ST_CP, Raspberry_Pi_1.GPIO6
  N11: U1.DS, Raspberry_Pi_1.GPIO4
  N12: U1.Q0, Q32.C
  VCC: U1.VCC, U2.VCC, U3.VCC, U4.VCC, U5.MR, U5.VCC, U6.MR, U6.VCC, U7.MR, U7.VCC, Raspberry_Pi_1.3v3
  N13: U2.Q1, Q39.C
  N14: U2.Q2, Q38.C
  N15: U2.Q3, Q37.C
  N16: U2.Q4, Q36.C
  N17: U2.Q5, Q35.C
  N18: U2.Q6, Q34.C
  N19: U2.Q7, Q33.C
  N20: U2.Q7', U3.DS
  N21: U2.Q0, Q40.C
  N22: U3.Q1, Q15.C
  N23: U3.Q2, Q14.C
  N24: U3.Q3, Q13.C
  N25: U3.Q4, Q12.C
  N26: U3.Q5, Q11.C
  N27: U3.Q6, Q19.C
  N28: U3.Q7, Q20.C
  N29: U3.Q7', U4.DS
  N30: U3.Q0, Q16.C
  N31: U4.Q1, Q25.C
  N32: U4.Q2, Q24.C
  N33: U4.Q3, Q23.C
  N34: U4.Q4, Q22.C
  N35: U4.Q5, Q21.C
  N36: U4.Q6, Q18.C
  N37: U4.Q7, Q17.C
  N38: U4.Q7', U5.DS
  N39: U4.Q0, Q26.C
  N40: U5.Q1, Q50.C
  N41: U5.Q2, Q52.C
  N42: U5.Q3, Q49.C
  N43: U5.Q4, Q54.C
  N44: U5.Q5, Q55.C
  N45: U5.Q6, Q56.C
  N46: U5.Q7, Q62.C
  N47: U5.Q7', U6.DS
  N48: U5.Q0, Q46.C
  N49: U6.Q1, Q7.C
  N50: U6.Q2, Q5.C
  N51: U6.Q3, Q4.C
  N52: U6.Q4, Q6.C
  N53: U6.Q5, Q10.C
  N54: U6.Q6, Q44.C
  N55: U6.Q7, Q47.C
  N56: U6.Q7', U7.DS
  N57: U6.Q0, Q60.C
  N58: U7.Q1, Q61.C
  N59: U7.Q2, Q57.C
  N60: U7.Q3, Q45.C
  N61: U7.Q4, Q3.C
  N62: U7.Q5, Q58.C
  N63: U7.Q6, Q59.C
  N64: U7.Q7, Q8.C
  N65: U7.Q0, Q63.C
  N66: Q49.E, Q52.E
