# Fritzing sketch circuitoMain3 (saved by Fritzing 0.9.3b)
circuit board: 30cm x 20cm
breadboards: 1

parts:
  U1 = 74HC595 [package="DIP16 [THT]"]
  U2 = 74HC595 [package="DIP16 [THT]"]
  U3 = 74HC595 [package="DIP16 [THT]"]
  U4 = 74HC595 [package="DIP16 [THT]"]
  U5 = 74HC595 [package="DIP16 [THT]"]
  U6 = 74HC595 [package="DIP16 [THT]"]
  U7 = 74HC595 [package="DIP16 [THT]"]
  Q3 = PNP-Transistor [package="TO92 [THT]"]
  Q4 = PNP-Transistor [package="TO92 [THT]"]
  Q5 = PNP-Transistor [package="TO92 [THT]"]
  Q6 = PNP-Transistor [package="TO92 [THT]"]
  Q7 = PNP-Transistor [package="TO92 [THT]"]
  Q8 = PNP-Transistor [package="TO92 [THT]"]
  Q10 = PNP-Transistor [package="TO92 [THT]"]
  Q11 = PNP-Transistor [package="TO92 [THT]"]
  Q12 = PNP-Transistor [package="TO92 [THT]"]
  Q13 = PNP-Transistor [package="TO92 [THT]"]
  Q14 = PNP-Transistor [package="TO92 [THT]"]
  Q15 = PNP-Transistor [package="TO92 [THT]"]
  Q16 = PNP-Transistor [package="TO92 [THT]"]
  Q17 = PNP-Transistor [package="TO92 [THT]"]
  Q18 = PNP-Transistor [package="TO92 [THT]"]
  Q19 = PNP-Transistor [package="TO92 [THT]"]
  Q20 = PNP-Transistor [package="TO92 [THT]"]
  Q21 = PNP-Transistor [package="TO92 [THT]"]
  Q22 = PNP-Transistor [package="TO92 [THT]"]
  Q23 = PNP-Transistor [package="TO92 [THT]"]
  Q24 = PNP-Transistor [package="TO92 [THT]"]
  Q25 = PNP-Transistor [package="TO92 [THT]"]
  Q26 = PNP-Transistor [package="TO92 [THT]"]
  Q27 = PNP-Transistor [package="TO92 [THT]"]
  Q28 = PNP-Transistor [package="TO92 [THT]"]
  Q30 = PNP-Transistor [package="TO92 [THT]"]
  Q31 = PNP-Transistor [package="TO92 [THT]"]
  Q32 = PNP-Transistor [package="TO92 [THT]"]
  Q33 = PNP-Transistor [package="TO92 [THT]"]
  Q34 = PNP-Transistor [package="TO92 [THT]"]
  Q35 = PNP-Transistor [package="TO92 [THT]"]
  Q36 = PNP-Transistor [package="TO92 [THT]"]
  Q37 = PNP-Transistor [package="TO92 [THT]"]
  Q38 = PNP-Transistor [package="TO92 [THT]"]
  Q39 = PNP-Transistor [package="TO92 [THT]"]
  Q40 = PNP-Transistor [package="TO92 [THT]"]
  Q41 = PNP-Transistor [package="TO92 [THT]"]
  Q42 = PNP-Transistor [package="TO92 [THT]"]
  Q43 = PNP-Transistor [package="TO92 [THT]"]
  Q44 = PNP-Transistor [package="TO92 [THT]"]
  Q45 = PNP-Transistor [package="TO92 [THT]"]
  Q46 = PNP-Transistor [package="TO92 [THT]"]
  Q47 = PNP-Transistor [package="TO92 [THT]"]
  Q49 = PNP-Transistor [package="TO92 [THT]"]
  Q50 = PNP-Transistor [package="TO92 [THT]"]
  Q52 = PNP-Transistor [package="TO92 [THT]"]
  Q54 = PNP-Transistor [package="TO92 [THT]"]
  Q55 = PNP-Transistor [package="TO92 [THT]"]
  Q56 = PNP-Transistor [package="TO92 [THT]"]
  Q57 = PNP-Transistor [package="TO92 [THT]"]
  Q58 = PNP-Transistor [package="TO92 [THT]"]
  Q59 = PNP-Transistor [package="TO92 [THT]"]
  Q60 = PNP-Transistor [package="TO92 [THT]"]
  Q61 = PNP-Transistor [package="TO92 [THT]"]
  Q62 = PNP-Transistor [package="TO92 [THT]"]
  Q63 = PNP-Transistor [package="TO92 [THT]"]
  J1 = female pin header, 2 pins [form="♀ (female)"]
  J2 = female pin header, 2 pins [form="♀ (female)"]
  J3 = female pin header, 2 pins [form="♀ (female)"]
  J4 = female pin header, 2 pins [form="♀ (female)"]
  J5 = female pin header, 2 pins [form="♀ (female)"]
  J6 = female pin header, 2 pins [form="♀ (female)"]
  J7 = female pin header, 2 pins [form="♀ (female)"]
  J8 = female pin header, 2 pins [form="♀ (female)"]
  J9 = female pin header, 2 pins [form="♀ (female)"]
  J10 = female pin header, 2 pins [form="♀ (female)"]
  J11 = female pin header, 2 pins [form="♀ (female)"]
  J12 = female pin header, 2 pins [form="♀ (female)"]
  J13 = female pin header, 2 pins [form="♀ (female)"]
  J14 = female pin header, 2 pins [form="♀ (female)"]
  J15 = female pin header, 2 pins [form="♀ (female)"]
  J16 = female pin header, 2 pins [form="♀ (female)"]
  J17 = female pin header, 2 pins [form="♀ (female)"]
  J18 = female pin header, 2 pins [form="♀ (female)"]
  J19 = female pin header, 2 pins [form="♀ (female)"]
  J20 = female pin header, 2 pins [form="♀ (female)"]
  J21 = female pin header, 2 pins [form="♀ (female)"]
  J22 = female pin header, 2 pins [form="♀ (female)"]
  J23 = female pin header, 2 pins [form="♀ (female)"]
  J24 = female pin header, 2 pins [form="♀ (female)"]
  J25 = female pin header, 2 pins [form="♀ (female)"]
  J26 = female pin header, 2 pins [form="♀ (female)"]
  J27 = female pin header, 2 pins [form="♀ (female)"]
  J28 = female pin header, 2 pins [form="♀ (female)"]
  J29 = female pin header, 2 pins [form="♀ (female)"]
  J30 = female pin header, 2 pins [form="♀ (female)"]
  J31 = female pin header, 2 pins [form="♀ (female)"]
  J32 = female pin header, 2 pins [form="♀ (female)"]
  J33 = female pin header, 2 pins [form="♀ (female)"]
  J34 = female pin header, 2 pins [form="♀ (female)"]
  J35 = female pin header, 2 pins [form="♀ (female)"]
  J36 = female pin header, 2 pins [form="♀ (female)"]
  J37 = female pin header, 2 pins [form="♀ (female)"]
  J38 = female pin header, 2 pins [form="♀ (female)"]
  J39 = female pin header, 2 pins [form="♀ (female)"]
  J40 = female pin header, 2 pins [form="♀ (female)"]
  J41 = female pin header, 2 pins [form="♀ (female)"]
  J42 = female pin header, 2 pins [form="♀ (female)"]
  J43 = female pin header, 2 pins [form="♀ (female)"]
  J44 = female pin header, 2 pins [form="♀ (female)"]
  J45 = female pin header, 2 pins [form="♀ (female)"]
  J46 = female pin header, 2 pins [form="♀ (female)"]
  J47 = female pin header, 2 pins [form="♀ (female)"]
  J48 = female pin header, 2 pins [form="♀ (female)"]
  J49 = female pin header, 2 pins [form="♀ (female)"]
  J50 = female pin header, 2 pins [form="♀ (female)"]
  J51 = female pin header, 2 pins [form="♀ (female)"]
  J52 = female pin header, 2 pins [form="♀ (female)"]
  J53 = female pin header, 2 pins [form="♀ (female)"]
  J54 = female pin header, 2 pins [form="♀ (female)"]
  J55 = female pin header, 2 pins [form="♀ (female)"]
  J56 = female pin header, 2 pins [form="♀ (female)"]
  J57 = female pin header, 2 pins [form="♀ (female)"]
  R56 = Resistor [tolerance=±5% resistance=100 package="0402 [SMD]"]
  R55 = Resistor [tolerance=±5% resistance=100 package="0402 [SMD]"]
  R54 = Resistor [tolerance=±5% resistance=100 package="0402 [SMD]"]
  R53 = Resistor [tolerance=±5% resistance=100 package="0402 [SMD]"]
  R52 = Resistor [tolerance=±5% resistance=100 package="0402 [SMD]"]
  R51 = Resistor [tolerance=±5% resistance=100 package="0402 [SMD]"]
  R50 = Resistor [tolerance=±5% resistance=100 package="0402 [SMD]"]
  R49 = Resistor [tolerance=±5% resistance=100 package="0402 [SMD]"]
  R48 = Resistor [tolerance=±5% resistance=100 package="0402 [SMD]"]
  R47 = Resistor [tolerance=±5% resistance=100 package="0402 [SMD]"]
  R46 = Resistor [tolerance=±5% resistance=100 package="0402 [SMD]"]
  R45 = Resistor [tolerance=±5% resistance=100 package="0402 [SMD]"]
  R44 = Resistor [tolerance=±5% resistance=100 package="0402 [SMD]"]
  R43 = Resistor [tolerance=±5% resistance=100 package="0402 [SMD]"]
  R42 = Resistor [tolerance=±5% resistance=100 package="0402 [SMD]"]
  R41 = Resistor [tolerance=±5% resistance=100 package="0402 [SMD]"]
  R40 = Resistor [tolerance=±5% resistance=100 package="0402 [SMD]"]
  R39 = Resistor [tolerance=±5% resistance=100 package="0402 [SMD]"]
  R38 = Resistor [tolerance=±5% resistance=100 package="0402 [SMD]"]
  R37 = Resistor [tolerance=±5% resistance=100 package="0402 [SMD]"]
  R36 = Resistor [tolerance=±5% resistance=100 package="0402 [SMD]"]
  R35 = Resistor [tolerance=±5% resistance=100 package="0402 [SMD]"]
  R34 = Resistor [tolerance=±5% resistance=100 package="0402 [SMD]"]
  R33 = Resistor [tolerance=±5% resistance=100 package="0402 [SMD]"]
  R32 = Resistor [tolerance=±5% resistance=100 package="0402 [SMD]"]
  R31 = Resistor [tolerance=±5% resistance=100 package="0402 [SMD]"]
  R30 = Resistor [tolerance=±5% resistance=100 package="0402 [SMD]"]
  R29 = Resistor [tolerance=±5% resistance=100 package="0402 [SMD]"]
  R28 = Resistor [tolerance=±5% resistance=100 package="0402 [SMD]"]
  R27 = Resistor [tolerance=±5% resistance=100 package="0402 [SMD]"]
  R26 = Resistor [tolerance=±5% resistance=100 package="0402 [SMD]"]
  R25 = Resistor [tolerance=±5% resistance=100 package="0402 [SMD]"]
  R24 = Resistor [tolerance=±5% resistance=100 package="0402 [SMD]"]
  R23 = Resistor [tolerance=±5% resistance=100 package="0402 [SMD]"]
  R22 = Resistor [tolerance=±5% resistance=100 package="0402 [SMD]"]
  R21 = Resistor [tolerance=±5% resistance=100 package="0402 [SMD]"]
  R20 = Resistor [tolerance=±5% resistance=100 package="0402 [SMD]"]
  R19 = Resistor [tolerance=±5% resistance=100 package="0402 [SMD]"]
  R18 = Resistor [tolerance=±5% resistance=100 package="0402 [SMD]"]
  R17 = Resistor [tolerance=±5% resistance=100 package="0402 [SMD]"]
  R16 = Resistor [tolerance=±5% resistance=100 package="0402 [SMD]"]
  R15 = Resistor [tolerance=±5% resistance=100 package="0402 [SMD]"]
  R14 = Resistor [tolerance=±5% resistance=100 package="0402 [SMD]"]
  R13 = Resistor [tolerance=±5% resistance=100 package="0402 [SMD]"]
  R12 = Resistor [tolerance=±5% resistance=100 package="0402 [SMD]"]
  R11 = Resistor [tolerance=±5% resistance=100 package="0402 [SMD]"]
  R10 = Resistor [tolerance=±5% resistance=100 package="0402 [SMD]"]
  R9 = Resistor [tolerance=±5% resistance=100 package="0402 [SMD]"]
  R8 = Resistor [tolerance=±5% resistance=100 package="0402 [SMD]"]
  R7 = Resistor [tolerance=±5% resistance=100 package="0402 [SMD]"]
  R6 = Resistor [tolerance=±5% resistance=100 package="0402 [SMD]"]
  R5 = Resistor [tolerance=±5% resistance=100 package="0402 [SMD]"]
  R4 = Resistor [tolerance=±5% resistance=100 package="0402 [SMD]"]
  R3 = Resistor [tolerance=±5% resistance=100 package="0402 [SMD]"]
  R2 = Resistor [tolerance=±5% resistance=100 package="0402 [SMD]"]
  R1 = Resistor [tolerance=±5% resistance=100 package="0402 [SMD]"]
  J58 = female pin header, 5 pins [form="♀ (female)"]

nets:
  N1: U1.Q1, Q31.B
  N2: U1.Q2, Q30.B
  N3: U1.Q3, Q43.B
  N4: U1.Q4, Q28.B
  N5: U1.Q5, Q27.B
  N6: U1.Q6, Q41.B
  N7: U1.Q7, Q42.B
  GND: U1.GND, U1.OE, U2.GND, U2.OE, U3.GND, U3.OE, U4.GND, U4.OE, U5.GND, U5.OE, Q5.E, Q7.E, Q8.E, Q25.E, Q26.E, Q27.E, Q28.E, Q30.E, Q31.E, Q32.E, Q33.E, Q34.E, Q35.E, Q36.E, Q37.E, Q38.E, Q39.E, Q40.E, Q41.E, Q42.E, Q43.E, Q45.E, Q57.E, Q61.E, Q63.E, J57.pin1, J58.pin1
  N8: U1.Q7', U2.DS
  VCC: U1.MR, U1.VCC, U2.MR, U2.VCC, U3.MR, U3.VCC, U4.MR, U4.VCC, U5.MR, U5.VCC, J58.pin2
  N9: U1.SH_CP, U2.SH_CP, U3.SH_CP, U4.SH_CP, U5.SH_CP, U6.SH_CP, U7.SH_CP, J58.pin4
  N10: U1.ST_CP, U2.ST_CP, U3.ST_CP, U4.ST_CP, U5.ST_CP, U6.ST_CP, U7.ST_CP, J58.pin5
  N11: U1.DS, J58.pin3
  N12: U1.Q0, Q32.B
  N13: U2.Q1, Q39.B
  N14: U2.Q2, Q38.B
  N15: U2.Q3, Q37.B
  N16: U2.Q4, Q36.B
  N17: U2.Q5, Q35.B
  N18: U2.Q6, Q34.B
  N19: U2.Q7, Q33.B
  N20: U2.Q7', U3.DS
  N21: U2.Q0, Q40.B
  N22: U3.Q1, Q15.B
  N23: U3.Q2, Q14.B
  N24: U3.Q3, Q13.B
  N25: U3.Q4, Q12.B
  N26: U3.Q5, Q11.B
  N27: U3.Q6, Q19.B
  N28: U3.Q7, Q20.B
  N29: U3.Q7', U4.DS
  N30: U3.Q0, Q16.B
  N31: U4.Q1, Q25.B
  N32: U4.Q2, Q24.B
  N33: U4.Q3, Q23.B
  N34: U4.Q4, Q22.B
  N35: U4.Q5, Q21.B
  N36: U4.Q6, Q18.B
  N37: U4.Q7, Q17.B
  N38: U4.Q7', U5.DS
  N39: U4.Q0, Q26.B
  N40: U5.Q1, Q50.B
  N41: U5.Q2, Q52.B
  N42: U5.Q3, Q49.B
  N43: U5.Q4, Q54.B
  N44: U5.Q5, Q55.B
  N45: U5.Q6, Q56.B
  N46: U5.Q7, Q62.B
  N47: U5.Q7', U6.DS
  N48: U5.Q0, Q46.B
  N49: U6.Q1, Q7.B
  N50: U6.Q2, Q5.B
  N51: U6.Q3, Q4.B
  N52: U6.Q4, Q6.B
  N53: U6.Q5, Q10.B
  N54: U6.Q6, Q44.B
  N55: U6.Q7, Q47.B
  GND_2: U6.GND, U6.OE, U7.GND, U7.OE
  N56: U6.Q7', U7.DS
  VCC_2: U6.MR, U6.VCC, U7.MR, U7.VCC
  N57: U6.Q0, Q60.B
  N58: U7.Q1, Q61.B
  N59: U7.Q2, Q57.B
  N60: U7.Q3, Q45.B
  N61: U7.Q4, Q3.B
  N62: U7.Q5, Q58.B
  N63: U7.Q6, Q59.B
  N64: U7.Q7, Q8.B
  N65: U7.Q0, Q63.B
  N66: Q3.C, R4.Pin_1
  N67: Q4.C, R11.Pin_1
  N68: Q5.C, R10.Pin_1
  N69: Q6.C, R12.Pin_1
  N70: Q7.C, R9.Pin_1
  N71: Q8.C, R7.Pin_1
  N72: Q10.C, R13.Pin_1
  N73: Q11.C, J41.pin1
  N74: Q12.C, J42.pin1
  N75: Q13.C, J43.pin1
  N76: Q14.C, J44.pin1
  N77: Q15.C, J45.pin1
  N78: Q16.C, J46.pin1
  N79: Q17.C, J47.pin1
  N80: Q18.C, J48.pin1
  N81: Q19.C, J40.pin1
  N82: Q20.C, R38.Pin_0
  N83: Q21.C, J50.pin1
  N84: Q22.C, J49.pin1
  N85: Q23.C, J51.pin1
  N86: Q24.C, J52.pin1
  N87: Q25.C, J53.pin1
  N88: Q26.C, J54.pin1
  N89: Q27.C, R42.Pin_0
  N90: Q28.C, R43.Pin_0
  N91: Q30.C, R45.Pin_0
  N92: Q31.C, R46.Pin_0
  N93: Q32.C, R47.Pin_0
  N94: Q33.C, R49.Pin_0
  N95: Q34.C, R48.Pin_0
  N96: Q35.C, R50.Pin_0
  N97: Q36.C, R51.Pin_0
  N98: Q37.C, R52.Pin_0
  N99: Q38.C, R53.Pin_0
  N100: Q39.C, R54.Pin_0
  N101: Q40.C, R55.Pin_0
  N102: Q41.C, R41.Pin_0
  N103: Q42.C, R40.Pin_0
  N104: Q43.C, J27.pin2, R44.Pin_0, R44.Pin_1
  N105: Q44.C, R14.Pin_1
  N106: Q45.C, R3.Pin_1
  N107: Q46.C, R16.Pin_1
  N108: Q47.C, R15.Pin_1
  N109: Q49.E, Q52.E
  N110: Q49.C, R19.Pin_1
  N111: Q50.C, R17.Pin_1
  N112: Q52.C, R18.Pin_1
  N113: Q54.C, R20.Pin_1
  N114: Q55.C, R21.Pin_1
  N115: Q56.C, R22.Pin_1
  N116: Q57.C, R56.Pin_1
  N117: Q58.C, R5.Pin_1
  N118: Q59.C, R6.Pin_1
  N119: Q60.C, R8.Pin_1
  N120: Q61.C, R2.Pin_1
  N121: Q62.C, R23.Pin_1
  N122: Q63.C, R1.Pin_0
  N123: J1.pin1, R1.Pin_1
  N124: J1.pin2, J2.pin2, J3.pin2, J4.pin2, J5.pin2, J6.pin2, J7.pin2, J8.pin2, J9.pin2, J10.pin2, J11.pin2, J12.pin2, J13.pin2, J14.pin2, J15.pin2, J16.pin2, J17.pin2, J18.pin2, J19.pin2, J20.pin2, J21.pin2, J22.pin2, J23.pin1, J35.pin1, J37.pin1, J38.pin1, J39.pin2, J55.pin2, J56.pin2, J57.pin2, R39.Pin_1, R37.Pin_1, R36.Pin_1, R35.Pin_1, R34.Pin_1, R33.Pin_1, R32.Pin_1, R31.Pin_1, R30.Pin_1, R29.Pin_1, R28.Pin_1, R27.Pin_1, R26.Pin_1, R25.Pin_1, R24.Pin_1
  N125: J2.pin1, R2.Pin_0
  N126: J3.pin1, R3.Pin_0
  N127: J4.pin1, R4.Pin_0
  N128: J5.pin1, R5.Pin_0
  N129: J6.pin1, R6.Pin_0
  N130: J7.pin1, R7.Pin_0
  N131: J8.pin1, R8.Pin_0
  N132: J9.pin1, R12.Pin_0
  N133: J10.pin1, R9.Pin_0
  N134: J11.pin1, R10.Pin_0
  N135: J12.pin1, R11.Pin_0
  N136: J13.pin1, R13.Pin_0
  N137: J14.pin1, R14.Pin_0
  N138: J15.pin1, R15.Pin_0
  N139: J16.pin1, R16.Pin_0
  N140: J17.pin1, R17.Pin_0
  N141: J18.pin1, R18.Pin_0
  N142: J19.pin1, R19.Pin_0
  N143: J20.pin1, R20.Pin_0
  N144: J21.pin1, R21.Pin_0
  N145: J22.pin1, R22.Pin_0
  N146: J23.pin2, R40.Pin_1
  N147: J24.pin2, R41.Pin_1
  N148: J25.pin2, R42.Pin_1
  N149: J26.pin2, R43.Pin_1
  N150: J28.pin2, R45.Pin_1
  N151: J29.pin2, R46.Pin_1
  N152: J30.pin2, R47.Pin_1
  N153: J31.pin2, R49.Pin_1
  N154: J32.pin2, R48.Pin_1
  N155: J33.pin2, R50.Pin_1
  N156: J34.pin2, R51.Pin_1
  N157: J35.pin2, R52.Pin_1
  N158: J36.pin2, R53.Pin_1
  N159: J37.pin2, R54.Pin_1
  N160: J38.pin2, R55.Pin_1
  N161: J39.pin1, R38.Pin_1
  N162: J40.pin2, R39.Pin_0
  N163: J41.pin2, R37.Pin_0
  N164: J42.pin2, R36.Pin_0
  N165: J43.pin2, R35.Pin_0
  N166: J44.pin2, R34.Pin_0
  N167: J45.pin2, R33.Pin_0
  N168: J46.pin2, R32.Pin_0
  N169: J47.pin2, R31.Pin_0
  N170: J48.pin2, R30.Pin_0
  N171: J49.pin2, R28.Pin_0
  N172: J50.pin2, R29.Pin_0
  N173: J51.pin2, R27.Pin_0
  N174: J52.pin2, R26.Pin_0
  N175: J53.pin2, R25.Pin_0
  N176: J54.pin2, R24.Pin_0
  N177: J55.pin1, R23.Pin_0
  N178: J56.pin1, R56.Pin_0

notes:
  SHIFT CLOCK
  LATCH CLOCK
  GROUND
  VCC
  DATA
  PROJETO AURA - MEDIA LAB UnB
